// Logisim project PLDs.circ as structural Verilog: 32 circuits, main circuit PLD_PC_BUS
module PLD_PC_BUS (
  input  t0,
  input  t2,
  output PC_Bus
);

  or or_1 (PC_Bus, t0, t2);

  // Notes on the sheet:
  //   CLA 8
  //   PLDs
endmodule

module PLD_AR_LD (
  input  clock,
  input  t0,
  input  t2,
  input  t4,
  input  d1,
  input  d2,
  output AR_LD
);

  wire and_1_out, and_2_out, and_3_out, not_1_out, or_1_out;

  not not_1 (not_1_out, clock);
  or or_1 (or_1_out, d1, d2);
  and and_1 (and_1_out, t0, not_1_out);
  and and_2 (and_2_out, t2, not_1_out);
  and and_3 (and_3_out, t4, or_1_out, not_1_out);
  or or_2 (AR_LD, and_1_out, and_2_out, and_3_out);

  // Notes on the sheet:
  //   CLA 8
  //   PLDs
endmodule

module PLD_PC_LD (
  input  clock,
  input  t4,
  input  d5,
  input  d6,
  input  z,
  output PC_LD
);

  wire and_1_out, not_1_out, or_1_out;

  not not_1 (not_1_out, clock);
  and and_1 (and_1_out, d6, z);
  or or_1 (or_1_out, d5, and_1_out);
  and and_2 (PC_LD, t4, or_1_out, not_1_out);

  // Notes on the sheet:
  //   CLA 8
  //   PLDs
endmodule

module PLD_PC_INC (
  input  clock,
  input  t1,
  input  t3,
  input  d1,
  input  d2,
  input  d6,
  input  z,
  output PC_INC
);

  wire and_1_out, and_2_out, and_3_out, not_1_out, not_2_out, or_1_out;

  not not_1 (not_1_out, clock);
  not not_2 (not_2_out, z);
  and and_1 (and_1_out, d6, not_2_out);
  or or_1 (or_1_out, d1, d2, and_1_out);
  and and_2 (and_2_out, not_1_out, t1);
  or or_2 (PC_INC, and_2_out, and_3_out);
  and and_3 (and_3_out, t3, not_1_out, or_1_out);

  // Notes on the sheet:
  //   CLA 8
  //   PLDs
endmodule

module PLD_DR_LD (
  input  clock,
  input  t1,
  input  t3,
  input  t5,
  input  d1,
  input  d2,
  input  d5,
  input  d6,
  input  z,
  output DR_LD
);

  wire sbc_dr_ld1_1_dr_ld, sbc_dr_ld2_1_dr_ld2;

  SBC_DR_LD1 sbc_dr_ld1_1 (.clock(clock), .t1(t1), .t3(t3), .t5(t5), .d1(d1), .d2(d2), .DR_LD(sbc_dr_ld1_1_dr_ld));
  SBC_DR_LD2 sbc_dr_ld2_1 (.t3(t3), .d5(d5), .d6(d6), .z(z), .DR_LD2(sbc_dr_ld2_1_dr_ld2));
  or or_1 (DR_LD, sbc_dr_ld1_1_dr_ld, sbc_dr_ld2_1_dr_ld2);

  // Notes on the sheet:
  //   CLA 8
  //   PLDs
endmodule

module SBC_DR_LD1 (
  input  clock,
  input  t1,
  input  t3,
  input  t5,
  input  d1,
  input  d2,
  output DR_LD
);

  wire and_1_out, not_1_out, or_1_out, or_2_out, or_3_out;

  not not_1 (not_1_out, clock);
  or or_1 (or_1_out, t3, t5);
  or or_2 (or_2_out, d1, d2);
  and and_1 (and_1_out, or_1_out, or_2_out);
  and and_2 (DR_LD, not_1_out, or_3_out);
  or or_3 (or_3_out, t1, and_1_out);
endmodule

module SBC_DR_LD2 (
  input  t3,
  input  d5,
  input  d6,
  input  z,
  output DR_LD2
);

  wire and_1_out, or_1_out;

  and and_1 (and_1_out, z, d6);
  or or_1 (or_1_out, d5, and_1_out);
  and and_2 (DR_LD2, t3, or_1_out);
endmodule

module PLD_DR_BUS (
  input  t4,
  input  t6,
  input  d1,
  input  d2,
  input  d5,
  input  d6,
  input  z,
  output DR_BUS_OUT
);

  wire sbc_dr_bus1_1_dr_bus1, sbc_dr_bus2_1_dr_bus2;

  SBC_DR_BUS1 sbc_dr_bus1_1 (.t4(t4), .t6(t6), .d1(d1), .d2(d2), .d5(d5), .DR_BUS1(sbc_dr_bus1_1_dr_bus1));
  SBC_DR_BUS2 sbc_dr_bus2_1 (.t4(t4), .d6(d6), .z(z), .DR_BUS2(sbc_dr_bus2_1_dr_bus2));
  or or_1 (DR_BUS_OUT, sbc_dr_bus1_1_dr_bus1, sbc_dr_bus2_1_dr_bus2);

  // Notes on the sheet:
  //   CLA 8
  //   PLDs
endmodule

module SBC_DR_BUS1 (
  input  t4,
  input  t6,
  input  d1,
  input  d2,
  input  d5,
  output DR_BUS1
);

  wire and_1_out, and_2_out, or_1_out, or_2_out;

  or or_1 (or_1_out, d1, d2);
  or or_2 (or_2_out, t6, t4);
  and and_1 (and_1_out, or_1_out, or_2_out);
  and and_2 (and_2_out, d5, t4);
  or or_3 (DR_BUS1, and_1_out, and_2_out);
endmodule

module SBC_DR_BUS2 (
  input  t4,
  input  d6,
  input  z,
  output DR_BUS2
);

  and and_1 (DR_BUS2, z, d6, t4);
endmodule

module PLD_R_LD (
  input  clock,
  input  t3,
  input  d3,
  output R_LD
);

  wire not_1_out;

  not not_1 (not_1_out, clock);
  and and_1 (R_LD, t3, d3, not_1_out);

  // Notes on the sheet:
  //   CLA 8
  //   PLDs
endmodule

module PLD_R_BUS (
  input  t3,
  input  d4,
  input  d8,
  input  d9,
  input  d12,
  input  d13,
  output R_BUS
);

  wire or_1_out;

  or or_1 (or_1_out, d4, d8, d9, d12, d13);
  and and_1 (R_BUS, t3, or_1_out);

  // Notes on the sheet:
  //   CLA 8
  //   PLDs
endmodule

module PLD_S_LD (
  input  clock,
  input  t3,
  input  d0,
  output S_LD
);

  wire not_1_out;

  not not_1 (not_1_out, clock);
  and and_1 (S_LD, t3, d0, not_1_out);

  // Notes on the sheet:
  //   CLA 8
  //   PLDs
endmodule

module PLD_ACC_CLR (
  input  t3,
  input  d11,
  output ACC_CLR
);

  and and_1 (ACC_CLR, t3, d11);

  // Notes on the sheet:
  //   CLA 8
  //   PLDs
endmodule

module PLD_ACC_LD (
  input  clock,
  input  t3,
  input  t6,
  input  d1,
  input  d4,
  input  d8,
  input  d9,
  input  d10,
  input  d12,
  input  d13,
  input  d14,
  input  d15,
  output ACC_LD
);

  wire and_1_out, and_2_out, not_1_out, or_1_out, or_2_out;

  not not_1 (not_1_out, clock);
  or or_1 (or_1_out, d13, d4, d8, d9, d10, d12, d14, d15);
  and and_1 (and_1_out, t6, d1);
  and and_2 (and_2_out, t3, or_1_out);
  or or_2 (or_2_out, and_1_out, and_2_out);
  and and_3 (ACC_LD, not_1_out, or_2_out);

  // Notes on the sheet:
  //   CLA 8
  //   PLDs
endmodule

module SBC_ACC_LD1 (
  input  t3,
  input  d4,
  input  d8,
  input  d9,
  input  d10,
  input  d12,
  input  d13,
  input  d14,
  input  d15,
  output ACC_LD
);

  wire or_1_out;

  or or_1 (or_1_out, d13, d4, d8, d9, d10, d12, d14, d15);
  and and_1 (ACC_LD, t3, or_1_out);

  // Notes on the sheet:
  //   CLA 8
  //   PLDs
endmodule

module PLD_ACC_BUS (
  input  t3,
  input  t5,
  input  d2,
  input  d3,
  input  d7,
  output ACC_Bus
);

  wire and_1_out, and_2_out, or_1_out;

  or or_1 (or_1_out, d3, d7);
  and and_1 (and_1_out, t3, or_1_out);
  and and_2 (and_2_out, t5, d2);
  or or_2 (ACC_Bus, and_1_out, and_2_out);

  // Notes on the sheet:
  //   CLA 8
  //   PLDs
endmodule

module PLD_ALU_SEL (
  input  d1,
  input  d4,
  input  d9,
  input  d10,
  input  d12,
  input  d13,
  input  d14,
  input  d15,
  output [2:0] s0
);

  SBC_ALU_SEL0 sbc_alu_sel0_1 (.d1(d1), .d4(d4), .d9(d9), .d13(d13), .d15(d15), .s0(s0[0]));
  SBC_ALU_SEL1 sbc_alu_sel1_1 (.d1(d1), .d4(d4), .d10(d10), .d14(d14), .d15(d15), .s1(s0[1]));
  SBC_ALU_SEL2 sbc_alu_sel2_1 (.d12(d12), .d13(d13), .d14(d14), .d15(d15), .s2(s0[2]));

  // Notes on the sheet:
  //   CLA 8
  //   PLDs
endmodule

module SBC_ALU_SEL0 (
  input  d1,
  input  d4,
  input  d9,
  input  d13,
  input  d15,
  output s0
);

  or or_1 (s0, d1, d4, d9, d13, d15);

  // Notes on the sheet:
  //   CLA 8
  //   PLDs
endmodule

module SBC_ALU_SEL1 (
  input  d1,
  input  d4,
  input  d10,
  input  d14,
  input  d15,
  output s1
);

  or or_1 (s1, d1, d4, d10, d14, d15);

  // Notes on the sheet:
  //   CLA 8
  //   PLDs
endmodule

module SBC_ALU_SEL2 (
  input  d12,
  input  d13,
  input  d14,
  input  d15,
  output s2
);

  or or_1 (s2, d12, d13, d14, d15);

  // Notes on the sheet:
  //   CLA 8
  //   PLDs
endmodule

module PLD_Z_LD (
  input  clock,
  output Z_LD
);

  wire not_1_out;

  not not_1 (not_1_out, clock);
  and and_1 (Z_LD, 1'b1, not_1_out);

  // Notes on the sheet:
  //   CLA 8
  //   PLDs
endmodule

module PLD_OUTR_LD (
  input  clock,
  input  t3,
  input  d7,
  output OUTR_LD
);

  wire not_1_out;

  not not_1 (not_1_out, clock);
  and and_1 (OUTR_LD, t3, d7, not_1_out);

  // Notes on the sheet:
  //   CLA 8
  //   PLDs
endmodule

module PLD_RAM_WE (
  input  clock,
  input  t6,
  input  d2,
  output RAM_WE
);

  wire not_1_out;

  not not_1 (not_1_out, clock);
  and and_1 (RAM_WE, t6, d2, not_1_out);

  // Notes on the sheet:
  //   CLA 8
  //   PLDs
endmodule

module PLD_RAM_OE (
  input  clock,
  input  t1,
  input  t3,
  input  t5,
  input  d1,
  input  d2,
  input  d5,
  input  d6,
  input  z,
  output RAM_OE
);

  wire not_1_out, or_1_out, sbc_ram_oe1_1_ram_oe, sbc_ram_oe2_1_ram_oe;

  not not_1 (not_1_out, clock);
  SBC_RAM_OE2 sbc_ram_oe2_1 (.t1(t1), .t3(t3), .d2(d2), .d5(d5), .d6(d6), .z(z), .RAM_OE(sbc_ram_oe2_1_ram_oe));
  SBC_RAM_OE1 sbc_ram_oe1_1 (.t3(t3), .t5(t5), .d1(d1), .RAM_OE(sbc_ram_oe1_1_ram_oe));
  or or_1 (or_1_out, sbc_ram_oe2_1_ram_oe, sbc_ram_oe1_1_ram_oe);
  and and_1 (RAM_OE, not_1_out, or_1_out);

  // Notes on the sheet:
  //   CLA 8
  //   PLDs
endmodule

module SBC_RAM_OE1 (
  input  t3,
  input  t5,
  input  d1,
  output RAM_OE
);

  wire or_1_out;

  or or_1 (or_1_out, t5, t3);
  and and_1 (RAM_OE, or_1_out, d1);
endmodule

module SBC_RAM_OE2 (
  input  t1,
  input  t3,
  input  d2,
  input  d5,
  input  d6,
  input  z,
  output RAM_OE
);

  wire and_1_out, and_2_out, or_1_out;

  and and_1 (and_1_out, d6, z);
  or or_1 (or_1_out, d2, d5, and_1_out);
  and and_2 (and_2_out, t3, or_1_out);
  or or_2 (RAM_OE, and_2_out, t1);
endmodule

module PLD_IR_LD (
  input  clock,
  input  t2,
  output IR_LD
);

  wire not_1_out;

  not not_1 (not_1_out, clock);
  and and_1 (IR_LD, t2, not_1_out);

  // Notes on the sheet:
  //   CLA 8
  //   PLDs
endmodule

module PLD_SC_CLR (
  input  t4,
  input  t5,
  input  t7,
  input  d0,
  input  d1,
  input  d2,
  input  d5,
  input  d6,
  input  z,
  output SC_CLR
);

  wire sbc_sc_clr1_1_sbc_clr1, sbc_sc_clr2_1_sbc_clr2, sbc_sc_clr3_1_sbc_clr3;

  SBC_SC_CLR2 sbc_sc_clr2_1 (.t4(t4), .d0(d0), .d2(d2), .d5(d5), .d6(d6), .z(z), .SBC_CLR2(sbc_sc_clr2_1_sbc_clr2));
  SBC_SC_CLR3 sbc_sc_clr3_1 (.t5(t5), .d5(d5), .d6(d6), .z(z), .SBC_CLR3(sbc_sc_clr3_1_sbc_clr3));
  SBC_SC_CLR1 sbc_sc_clr1_1 (.t7(t7), .d1(d1), .d2(d2), .SBC_CLR1(sbc_sc_clr1_1_sbc_clr1));
  or or_1 (SC_CLR, sbc_sc_clr2_1_sbc_clr2, sbc_sc_clr3_1_sbc_clr3, sbc_sc_clr1_1_sbc_clr1);

  // Notes on the sheet:
  //   CLA 8
  //   PLDs
endmodule

module SBC_SC_CLR1 (
  input  t7,
  input  d1,
  input  d2,
  output SBC_CLR1
);

  wire or_1_out;

  or or_1 (or_1_out, d1, d2);
  and and_1 (SBC_CLR1, t7, or_1_out);
endmodule

module SBC_SC_CLR2 (
  input  t4,
  input  d0,
  input  d2,
  input  d5,
  input  d6,
  input  z,
  output SBC_CLR2
);

  wire and_1_out, nor_1_out;

  and and_1 (and_1_out, z, d6);
  and and_2 (SBC_CLR2, t4, nor_1_out);
  nor nor_1 (nor_1_out, d0, d2, d5, and_1_out);
endmodule

module SBC_SC_CLR3 (
  input  t5,
  input  d5,
  input  d6,
  input  z,
  output SBC_CLR3
);

  wire and_1_out, or_1_out;

  and and_1 (and_1_out, z, d6);
  or or_1 (or_1_out, d5, and_1_out);
  and and_2 (SBC_CLR3, t5, or_1_out);
endmodule
