// Logisim project RSC.circ as structural Verilog: 10 circuits, main circuit Arith_U
// AU
module Arith_U (
  input  [31:0] A,
  input  [31:0] B,
  input  S1,
  input  S0,
  output [31:0] AU_out
);

  wire and_1_out, not_2_out;
  wire [31:0] adder_1_out, multiplexer_1_out, not_1_out;

  assign not_1_out = ~B;  // NOT_Gate not_1, 32 bits wide
  Multiplexer #(.select(2), .width(32)) multiplexer_1 (
    .in0(not_1_out), .in1(B), .in2({32{1'b0}}), .in3(B), .out(multiplexer_1_out), .sel({S1, S0}));
  Adder #(.width(32)) adder_1 (.a(A), .b(multiplexer_1_out), .out(adder_1_out), .cin(not_2_out));  // open: cout
  Multiplexer #(.width(32)) multiplexer_2 (.in0(adder_1_out), .in1(multiplexer_1_out), .out(AU_out), .sel(and_1_out));
  and and_1 (and_1_out, S1, S0);
  not not_2 (not_2_out, S0);

  // Notes on the sheet:
  //   Mac Reed
  //   Dakota Ponder
  //   CLA 4
  //   Arithmetic Unit
endmodule

module Logic_U (
  input  [31:0] B,
  input  [31:0] A,
  input  S1,
  input  S0,
  output [31:0] Logic_Out
);

  wire [31:0] and_1_out, not_1_out, or_1_out, shifter_1_out;

  assign and_1_out = B & A;  // AND_Gate and_1, 32 bits wide
  assign or_1_out = B | A;  // OR_Gate or_1, 32 bits wide
  assign not_1_out = ~A;  // NOT_Gate not_1, 32 bits wide
  Shifter #(.shift("ar"), .width(32)) shifter_1 (.in(A), .\dist (5'b00001), .out(shifter_1_out));
  Multiplexer #(.select(2), .width(32)) multiplexer_1 (
    .in0(and_1_out), .in1(or_1_out), .in2(shifter_1_out), .in3(not_1_out), .out(Logic_Out), .sel({S1, S0}));

  // Notes on the sheet:
  //   Mac Reed
  //   Dakota Ponder
  //   CLA 5
  //   ALU
endmodule

module ALU (
  input  [31:0] A,
  input  [31:0] B,
  input  S2,
  input  S1,
  input  S0,
  output [31:0] ALU_Out
);

  wire [31:0] arith_u_1_au_out, logic_u_1_logic_out;

  Arith_U arith_u_1 (.A(A), .B(B), .S1(S1), .S0(S0), .AU_out(arith_u_1_au_out));
  Logic_U logic_u_1 (.B(B), .A(A), .S1(S1), .S0(S0), .Logic_Out(logic_u_1_logic_out));
  Multiplexer #(.width(32)) multiplexer_1 (.in0(arith_u_1_au_out), .in1(logic_u_1_logic_out), .out(ALU_Out), .sel(S2));

  // Notes on the sheet:
  //   Mac Reed
  //   Dakota Ponder
  //   CLA 5
  //   ALU
endmodule

module SC (
  input  Clock,
  input  Clear,
  output [2:0] SEQ_Out
);

  wire [2:0] adder_1_out;

  Adder #(.width(3)) adder_1 (.a(SEQ_Out), .b(3'b001), .out(adder_1_out));  // open: cin, cout
  Register #(.width(3)) register_1 (.D(adder_1_out), .en(Clock), .clk(Clock), .Q(SEQ_Out), .clr(Clear));

  // Notes on the sheet:
  //   Mac Reed
  //   Dakota Ponder
  //   CLA 6
  //   Sequence Counter
endmodule

module RSC (
  output [31:0] out_1,
  output [31:0] BUS_Out,
  output [31:0] PC_Out,
  output [31:0] DR_Out,
  output [31:0] R_Out,
  output [7:0] T,
  output [3:0] D,
  output [31:0] ACC_Out
);

  wire control_1_acc_bus, control_1_acc_clr, control_1_acc_ld, control_1_ar_ld, control_1_dr_bus,
       control_1_dr_ld, control_1_ir_ld, control_1_outr_ld, control_1_pc_bus, control_1_pc_inc,
       control_1_pc_ld, control_1_r_bus, control_1_r_ld, control_1_ram_oe, control_1_ram_we, control_1_z_ld,
       Primary_Clock_out, z_reg_1_z_out;
  wire [2:0] control_1_alu_s;
  wire [31:0] ALU_x_alu_out, ar_1_data_out, outr_1_data_out;

  IR ir_1 (.Data_In(DR_Out), .Load(control_1_ir_ld), .Clock(Primary_Clock_out), .Data_Out(out_1));
  Control control_1 (
    .Clock(Primary_Clock_out), .Z_In(z_reg_1_z_out), .IR_In(out_1), .IR_LD(control_1_ir_ld),
    .RAM_WE(control_1_ram_we), .RAM_OE(control_1_ram_oe), .AR_LD(control_1_ar_ld), .PC_LD(control_1_pc_ld),
    .T_Out(T), .PC_INC(control_1_pc_inc), .PC_BUS(control_1_pc_bus), .DR_LD(control_1_dr_ld),
    .DR_BUS(control_1_dr_bus), .D_Out(D), .R_LD(control_1_r_ld), .R_BUS(control_1_r_bus),
    .ACC_LD(control_1_acc_ld), .ACC_CLR(control_1_acc_clr), .ACC_BUS(control_1_acc_bus),
    .ALU_S(control_1_alu_s), .OUTR_LD(control_1_outr_ld), .Z_LD(control_1_z_ld));
  Z_Reg z_reg_1 (.Clock(Primary_Clock_out), .Load(control_1_z_ld), .ACC_in(ALU_x_alu_out), .Z_Out(z_reg_1_z_out));
  AR ar_1 (.Data_In(BUS_Out), .Load(control_1_ar_ld), .Clock(Primary_Clock_out), .Data_Out(ar_1_data_out));
  RAM #(.addrWidth(16), .dataWidth(32), .databus("bidir"), .trigger("high")) ram_1 (
    .addr(ar_1_data_out[15:0]), .we(control_1_ram_we), .oe(control_1_ram_oe), .data(BUS_Out));
  DR dr_1 (
    .Data_In(BUS_Out), .Load(control_1_dr_ld), .Clock(Primary_Clock_out), .Bus_Enable(control_1_dr_bus),
    .Data_Out(DR_Out), .Bus_Out(BUS_Out));
  R r_1 (
    .Data_In(BUS_Out), .Load(control_1_r_ld), .Clock(Primary_Clock_out), .Bus_Enable(control_1_r_bus),
    .Data_Out(R_Out), .Bus_Out(BUS_Out));
  // Probe on nothing
  ALU ALU_x (
    .A(ACC_Out), .B(BUS_Out), .S2(control_1_alu_s[2]), .S1(control_1_alu_s[1]), .S0(control_1_alu_s[0]),
    .ALU_Out(ALU_x_alu_out));
  Clock Primary_Clock (.out(Primary_Clock_out));
  // Probe on BUS_Out
  OUTR outr_1 (.Data_In(BUS_Out), .Load(control_1_outr_ld), .Clock(Primary_Clock_out), .Data_Out(outr_1_data_out));
  Hex_Digit_Display hex_digit_display_1 (.value(outr_1_data_out[31:28]));  // open: dp
  PC pc_1 (
    .Data_In(BUS_Out), .Count(control_1_pc_inc), .Load(control_1_pc_ld), .Clock(Primary_Clock_out),
    .Bus_Enable(control_1_pc_bus), .Data_Out(PC_Out), .Bus_Out(BUS_Out));
  ACC acc_1 (
    .Data_In(ALU_x_alu_out), .Load(control_1_acc_ld), .Clock(Primary_Clock_out), .Clear(control_1_acc_clr),
    .Bus_Enable(control_1_acc_bus), .Data_Out(ACC_Out), .Bus_Out(BUS_Out));
  Hex_Digit_Display hex_digit_display_2 (.value(outr_1_data_out[27:24]));  // open: dp
  Hex_Digit_Display hex_digit_display_3 (.value(outr_1_data_out[23:20]));  // open: dp
  // Probe on PC_Out
  // Probe on R_Out
  // Probe on ACC_Out
  Hex_Digit_Display hex_digit_display_4 (.value(outr_1_data_out[19:16]));  // open: dp
  Hex_Digit_Display hex_digit_display_5 (.value(outr_1_data_out[15:12]));  // open: dp
  Hex_Digit_Display hex_digit_display_6 (.value(outr_1_data_out[11:8]));  // open: dp
  Hex_Digit_Display hex_digit_display_7 (.value(outr_1_data_out[7:4]));  // open: dp
  Hex_Digit_Display hex_digit_display_8 (.value(outr_1_data_out[3:0]));  // open: dp

  // Notes on the sheet:
  //   Dakota Ponder 
  //   OLA 5
  //   Bus Loop and Memory
endmodule

module Z_Reg (
  input  Clock,
  input  Load,
  input  [31:0] ACC_in,
  output Z_Out
);

  wire not_1_out, or_2_out;
  wire [3:0] or_1_out;

  assign or_1_out = ACC_in[3:0] | ACC_in[7:4] | ACC_in[11:8] | ACC_in[15:12] | ACC_in[19:16] | ACC_in[23:20] | ACC_in[27:24] | ACC_in[31:28];  // OR_Gate or_1, 4 bits wide
  or or_2 (or_2_out, or_1_out[0], or_1_out[1], or_1_out[2], or_1_out[3]);
  not not_1 (not_1_out, or_2_out);
  Onebit_reg onebit_reg_1 (.Clock(Clock), .Data(not_1_out), .Load(Load), .Clear(1'b0), .Data_Out(Z_Out));
endmodule

module Control (
  input  Clock,
  input  Z_In,
  input  [31:0] IR_In,
  output IR_LD,
  output RAM_WE,
  output RAM_OE,
  output AR_LD,
  output PC_LD,
  output [7:0] T_Out,
  output PC_INC,
  output PC_BUS,
  output DR_LD,
  output DR_BUS,
  output [3:0] D_Out,
  output R_LD,
  output R_BUS,
  output ACC_LD,
  output ACC_CLR,
  output ACC_BUS,
  output [2:0] ALU_S,
  output OUTR_LD,
  output Z_LD
);

  wire pld_s_ld_1_s_ld, pld_sc_clr_1_sc_clr, s_reg_1_data_out;
  wire [15:0] decodercircuit_1_d_out;

  S_Reg s_reg_1 (.Clock(Clock), .Load(pld_s_ld_1_s_ld), .Data_Out(s_reg_1_data_out));  // open: Clear
  TimerCircuit timercircuit_1 (.Clock(Clock), .Stop(s_reg_1_data_out), .T_out(T_Out));  // open: Clear
  DecoderCircuit decodercircuit_1 (.IR_In(IR_In), .D_Out(decodercircuit_1_d_out), .Debug_Instruction(D_Out));
  PLD_IR_LD pld_ir_ld_1 (.clock(Clock), .t2(T_Out[2]), .IR_LD(IR_LD));
  PLD_RAM_WE pld_ram_we_1 (.clock(Clock), .t6(T_Out[6]), .d2(decodercircuit_1_d_out[2]), .RAM_WE(RAM_WE));
  PLD_RAM_OE pld_ram_oe_1 (
    .clock(Clock), .t1(T_Out[1]), .t3(T_Out[3]), .t5(T_Out[5]), .d1(decodercircuit_1_d_out[1]),
    .d2(decodercircuit_1_d_out[2]), .d5(decodercircuit_1_d_out[5]), .d6(decodercircuit_1_d_out[6]), .z(Z_In),
    .RAM_OE(RAM_OE));
  PLD_AR_LD pld_ar_ld_1 (
    .clock(Clock), .t0(T_Out[0]), .t2(T_Out[2]), .t4(T_Out[4]), .d1(decodercircuit_1_d_out[1]),
    .d2(decodercircuit_1_d_out[2]), .AR_LD(AR_LD));
  PLD_PC_LD pld_pc_ld_1 (
    .clock(Clock), .t4(T_Out[4]), .d5(decodercircuit_1_d_out[5]), .d6(decodercircuit_1_d_out[6]), .z(Z_In),
    .PC_LD(PC_LD));
  PLD_PC_INC pld_pc_inc_1 (
    .clock(Clock), .t1(T_Out[1]), .t3(T_Out[3]), .d1(decodercircuit_1_d_out[1]),
    .d2(decodercircuit_1_d_out[2]), .d6(decodercircuit_1_d_out[6]), .z(Z_In), .PC_INC(PC_INC));
  PLD_PC_BUS pld_pc_bus_1 (.t0(T_Out[0]), .t2(T_Out[2]), .PC_Bus(PC_BUS));
  PLD_DR_LD pld_dr_ld_1 (
    .clock(Clock), .t1(T_Out[1]), .t3(T_Out[3]), .t5(T_Out[5]), .d1(decodercircuit_1_d_out[1]),
    .d2(decodercircuit_1_d_out[2]), .d5(decodercircuit_1_d_out[5]), .d6(decodercircuit_1_d_out[6]), .z(Z_In),
    .DR_LD(DR_LD));
  PLD_DR_BUS pld_dr_bus_1 (
    .t4(T_Out[4]), .t6(T_Out[6]), .d1(decodercircuit_1_d_out[1]), .d2(decodercircuit_1_d_out[2]),
    .d5(decodercircuit_1_d_out[5]), .d6(decodercircuit_1_d_out[6]), .z(Z_In), .DR_BUS_OUT(DR_BUS));
  PLD_R_LD pld_r_ld_1 (.clock(Clock), .t3(T_Out[3]), .d3(decodercircuit_1_d_out[3]), .R_LD(R_LD));
  PLD_R_BUS pld_r_bus_1 (
    .t3(T_Out[3]), .d4(decodercircuit_1_d_out[4]), .d8(decodercircuit_1_d_out[8]),
    .d9(decodercircuit_1_d_out[9]), .d12(decodercircuit_1_d_out[12]), .d13(decodercircuit_1_d_out[13]),
    .R_BUS(R_BUS));
  PLD_ACC_LD pld_acc_ld_1 (
    .clock(Clock), .t3(T_Out[3]), .t6(T_Out[6]), .d1(decodercircuit_1_d_out[1]),
    .d4(decodercircuit_1_d_out[4]), .d8(decodercircuit_1_d_out[8]), .d9(decodercircuit_1_d_out[9]),
    .d10(decodercircuit_1_d_out[10]), .d12(decodercircuit_1_d_out[12]), .d13(decodercircuit_1_d_out[13]),
    .d14(decodercircuit_1_d_out[14]), .d15(decodercircuit_1_d_out[15]), .ACC_LD(ACC_LD));
  PLD_ACC_CLR pld_acc_clr_1 (.t3(T_Out[3]), .d11(decodercircuit_1_d_out[11]), .ACC_CLR(ACC_CLR));
  PLD_ACC_BUS pld_acc_bus_1 (
    .t3(T_Out[3]), .t5(T_Out[5]), .d2(decodercircuit_1_d_out[2]), .d3(decodercircuit_1_d_out[3]),
    .d7(decodercircuit_1_d_out[7]), .ACC_Bus(ACC_BUS));
  PLD_ALU_SEL pld_alu_sel_1 (
    .d1(decodercircuit_1_d_out[1]), .d4(decodercircuit_1_d_out[4]), .d9(decodercircuit_1_d_out[9]),
    .d10(decodercircuit_1_d_out[10]), .d12(decodercircuit_1_d_out[12]), .d13(decodercircuit_1_d_out[13]),
    .d14(decodercircuit_1_d_out[14]), .d15(decodercircuit_1_d_out[15]), .s0(ALU_S));
  PLD_OUTR_LD pld_outr_ld_1 (.clock(Clock), .t3(T_Out[3]), .d7(decodercircuit_1_d_out[7]), .OUTR_LD(OUTR_LD));
  PLD_Z_LD pld_z_ld_1 (.clock(Clock), .Z_LD(Z_LD));
  PLD_SC_CLR pld_sc_clr_1 (
    .t4(T_Out[4]), .t5(T_Out[5]), .t7(T_Out[7]), .d0(decodercircuit_1_d_out[0]),
    .d1(decodercircuit_1_d_out[1]), .d2(decodercircuit_1_d_out[2]), .d5(decodercircuit_1_d_out[5]),
    .d6(decodercircuit_1_d_out[6]), .z(Z_In), .SC_CLR(pld_sc_clr_1_sc_clr));
  PLD_S_LD pld_s_ld_1 (.clock(Clock), .t3(T_Out[3]), .d0(decodercircuit_1_d_out[0]), .S_LD(pld_s_ld_1_s_ld));
endmodule

module TimerCircuit (
  input  Clock,
  input  Clear,
  input  Stop,
  output [7:0] T_out
);

  wire not_1_out;
  wire [2:0] sc_1_seq_out;

  Decoder #(.select(3)) decoder_1 (
    .out0(T_out[0]), .out1(T_out[1]), .out2(T_out[2]), .out3(T_out[3]), .out4(T_out[4]), .out5(T_out[5]),
    .out6(T_out[6]), .out7(T_out[7]), .sel(sc_1_seq_out), .en(not_1_out));
  SC sc_1 (.Clock(Clock), .Clear(Clear), .SEQ_Out(sc_1_seq_out));
  not not_1 (not_1_out, Stop);
endmodule

module DecoderCircuit (
  input  [31:0] IR_In,
  output [15:0] D_Out,
  output [3:0] Debug_Instruction
);

  wire or_2_out;
  wire [3:0] or_1_out;
  wire [15:0] decoder_1_out0;

  assign or_1_out = IR_In[7:4] | IR_In[11:8] | IR_In[15:12] | IR_In[19:16] | IR_In[23:20] | IR_In[27:24] | IR_In[31:28];  // OR_Gate or_1, 4 bits wide
  Decoder #(.select(4)) decoder_1 (
    .out0(decoder_1_out0[0]), .out1(decoder_1_out0[1]), .out2(decoder_1_out0[2]), .out3(decoder_1_out0[3]),
    .out4(decoder_1_out0[4]), .out5(decoder_1_out0[5]), .out6(decoder_1_out0[6]), .out7(decoder_1_out0[7]),
    .out8(decoder_1_out0[8]), .out9(decoder_1_out0[9]), .out10(decoder_1_out0[10]),
    .out11(decoder_1_out0[11]), .out12(decoder_1_out0[12]), .out13(decoder_1_out0[13]),
    .out14(decoder_1_out0[14]), .out15(decoder_1_out0[15]), .sel(IR_In[3:0]));  // open: en
  or or_2 (or_2_out, or_1_out[0], or_1_out[1], or_1_out[2], or_1_out[3]);
  Multiplexer #(.width(16)) multiplexer_1 (.in0(decoder_1_out0), .in1({16{1'b0}}), .out(D_Out), .sel(or_2_out));

  assign Debug_Instruction = IR_In[3:0];
endmodule

module S_Reg (
  input  Clock,
  input  Load,
  input  Clear,
  output Data_Out
);

  wire and_1_out, and_2_out, not_1_out;

  and and_1 (and_1_out, 1'b1, Load);
  not not_1 (not_1_out, 1'b1);
  and and_2 (and_2_out, not_1_out, Load);
  J_K_Flip_Flop j_k_ff_1 (
    .J(and_1_out), .K(and_2_out), .clk(Clock), .Q(Data_Out), .preset(1'b0), .reset(Clear));  // open: Qn
endmodule
