// Logisim project custom_reg.circ as structural Verilog: 12 circuits, main circuit Onebit_reg
module Onebit_reg (
  input  Clock,
  input  Data,
  input  Load,
  input  Clear,
  output Data_Out
);

  wire and_1_out, and_2_out, not_1_out;

  and and_1 (and_1_out, Data, Load);
  not not_1 (not_1_out, Data);
  and and_2 (and_2_out, not_1_out, Load);
  J_K_Flip_Flop j_k_ff_1 (
    .J(and_1_out), .K(and_2_out), .clk(Clock), .Q(Data_Out), .preset(1'b0), .reset(Clear));  // open: Qn

  // Notes on the sheet:
  //   One bit Register
endmodule

module BasicRegister (
  input  [31:0] Data_In,
  input  Load,
  input  Clock,
  output [31:0] Data_Out
);

  Register #(.width(32)) register_1 (.D(Data_In), .en(Load), .clk(Clock), .Q(Data_Out));  // open: clr
endmodule

module BusRegister (
  input  [31:0] Data_In,
  input  Load,
  input  Clock,
  input  Bus_Enable,
  output [31:0] Data_Out,
  output [31:0] Bus_Out
);

  Register #(.width(32)) register_1 (.D(Data_In), .en(Load), .clk(Clock), .Q(Data_Out));  // open: clr
  assign Bus_Out = Bus_Enable ? Data_Out : 32'bz;  // Controlled_Buffer controlled_buffer_1
endmodule

module ClearRegister (
  input  [31:0] Data_In,
  input  Load,
  input  Clock,
  input  Clear,
  input  Bus_Enable,
  output [31:0] Data_Out,
  output [31:0] Bus_Out
);

  Register #(.width(32)) register_1 (.D(Data_In), .en(Load), .clk(Clock), .Q(Data_Out), .clr(Clear));
  assign Bus_Out = Bus_Enable ? Data_Out : 32'bz;  // Controlled_Buffer controlled_buffer_1
endmodule

module CountRegister (
  input  [31:0] Data_In,
  input  Count,
  input  Load,
  input  Clock,
  input  Bus_Enable,
  output [31:0] Data_Out,
  output [31:0] Bus_Out
);

  wire or_1_out;
  wire [31:0] adder_1_out, multiplexer_1_out;

  Adder #(.width(32)) adder_1 (.a(32'h1), .b(Data_Out), .out(adder_1_out));  // open: cin, cout
  or or_1 (or_1_out, Count, Load);
  Multiplexer #(.width(32)) multiplexer_1 (.in0(Data_In), .in1(adder_1_out), .out(multiplexer_1_out), .sel(Count));
  Register #(.width(32)) register_1 (.D(multiplexer_1_out), .en(or_1_out), .clk(Clock), .Q(Data_Out));  // open: clr
  assign Bus_Out = Bus_Enable ? Data_Out : 32'bz;  // Controlled_Buffer controlled_buffer_1
endmodule

module ACC (
  input  [31:0] Data_In,
  input  Load,
  input  Clock,
  input  Clear,
  input  Bus_Enable,
  output [31:0] Data_Out,
  output [31:0] Bus_Out
);

  ClearRegister clearregister_1 (
    .Data_In(Data_In), .Load(Load), .Clock(Clock), .Clear(Clear), .Bus_Enable(Bus_Enable),
    .Data_Out(Data_Out), .Bus_Out(Bus_Out));
endmodule

module AR (
  input  [31:0] Data_In,
  input  Load,
  input  Clock,
  output [31:0] Data_Out
);

  BasicRegister basicregister_1 (.Data_In(Data_In), .Load(Load), .Clock(Clock), .Data_Out(Data_Out));
endmodule

module DR (
  input  [31:0] Data_In,
  input  Load,
  input  Clock,
  input  Bus_Enable,
  output [31:0] Data_Out,
  output [31:0] Bus_Out
);

  BusRegister busregister_1 (
    .Data_In(Data_In), .Load(Load), .Clock(Clock), .Bus_Enable(Bus_Enable), .Data_Out(Data_Out),
    .Bus_Out(Bus_Out));
endmodule

module IR (
  input  [31:0] Data_In,
  input  Load,
  input  Clock,
  output [31:0] Data_Out
);

  BasicRegister basicregister_1 (.Data_In(Data_In), .Load(Load), .Clock(Clock), .Data_Out(Data_Out));
endmodule

module OUTR (
  input  [31:0] Data_In,
  input  Load,
  input  Clock,
  output [31:0] Data_Out
);

  BasicRegister basicregister_1 (.Data_In(Data_In), .Load(Load), .Clock(Clock), .Data_Out(Data_Out));
endmodule

module PC (
  input  [31:0] Data_In,
  input  Count,
  input  Load,
  input  Clock,
  input  Bus_Enable,
  output [31:0] Data_Out,
  output [31:0] Bus_Out
);

  CountRegister countregister_1 (
    .Data_In(Data_In), .Count(Count), .Load(Load), .Clock(Clock), .Bus_Enable(Bus_Enable),
    .Data_Out(Data_Out), .Bus_Out(Bus_Out));
endmodule

module R (
  input  [31:0] Data_In,
  input  Load,
  input  Clock,
  input  Bus_Enable,
  output [31:0] Data_Out,
  output [31:0] Bus_Out
);

  BusRegister busregister_1 (
    .Data_In(Data_In), .Load(Load), .Clock(Clock), .Bus_Enable(Bus_Enable), .Data_Out(Data_Out),
    .Bus_Out(Bus_Out));
endmodule
